// Logisim project CPU.circ as structural Verilog: 6 circuits, main circuit main
// address
module main (
  input  reset
);

  wire c, clock_1_out, clock_2_out, datawrite, dwrite, imload, irload, n, not_1_out, pcload, swrite, z;
  wire [1:0] addrsel, datasel, op2sel, pcsel, regsrc;
  wire [2:0] insrtuction_register_1_dregsel, insrtuction_register_1_sregsel, insrtuction_register_1_tregsel;
  wire [3:0] aluop;
  wire [6:0] opcode;
  wire [7:0] control_unit_1_ucounter;
  wire [15:0] aluout, dreg, immed, multiplexer_1_out, multiplexer_2_out, multiplexer_3_out,
       multiplexer_4_out, pc, ram_1_data, register_file_1_r0, register_file_1_r1, register_file_1_r2,
       register_file_1_r3, register_file_1_r4, register_file_1_r5, register_file_1_r6, register_file_1_r7,
       sreg, treg;

  Clock clock_1 (.out(clock_1_out));
  // Probe on control_unit_1_ucounter
  // Probe on c
  Control_Unit control_unit_1 (
    .opcode(opcode), .aluop(aluop), .op2sel(op2sel), .datawrite(datawrite), .addrsel(addrsel), .pcsel(pcsel),
    .pcload(pcload), .dwrite(dwrite), .irload(irload), .imload(imload), .regsrc(regsrc),
    .ucounter(control_unit_1_ucounter), .datasel(datasel), .swrite(swrite));
  // Probe on z
  // Probe on n
  // Probe on opcode
  RAM #(.addrWidth(16), .dataWidth(16)) ram_1 (
    .addr(multiplexer_1_out), .data(ram_1_data), .clk(clock_1_out), .ld(not_1_out));  // open: sel, clr
  not not_1 (not_1_out, datawrite);
  // Probe on aluop
  // Probe on op2sel
  // Probe on datawrite
  // Probe on addrsel
  // Probe on pcsel
  // Probe on pcload
  // Probe on dwrite
  // Probe on irload
  // Probe on imload
  // Probe on regsrc
  // Probe on datasel
  // Probe on swrite
  // Probe on multiplexer_1_out
  // Probe on ram_1_data
  Multiplexer #(.select(2), .width(16), .enable("false")) multiplexer_1 (
    .in0(pc), .in1(immed), .out(multiplexer_1_out), .sel(addrsel));  // open: in2, in3
  Register #(.width(16)) register_1 (.D(ram_1_data), .en(imload), .Q(immed), .clk(clock_2_out));  // open: clr
  Clock clock_2 (.out(clock_2_out));
  assign ram_1_data = datawrite ? multiplexer_2_out : 16'bz;  // Controlled_Buffer controlled_buffer_1
  Multiplexer #(.select(2), .width(16), .enable("false")) multiplexer_2 (
    .in1(dreg), .in2(treg), .in3(aluout), .out(multiplexer_2_out), .sel(datasel));  // open: in0
  // Probe on pc
  Program_Counter program_counter_1 (.imreg(immed), .pcout(pc), .pcsel(pcsel), .pcload(pcload), .reset(reset));
  Multiplexer #(.select(2), .width(16), .enable("false")) multiplexer_3 (
    .in0(ram_1_data), .in1(immed), .in2(aluout), .in3(sreg), .out(multiplexer_3_out), .sel(regsrc));
  Insrtuction_Register insrtuction_register_1 (
    .instruction(ram_1_data), .irload(irload), .dregsel(insrtuction_register_1_dregsel),
    .sregsel(insrtuction_register_1_sregsel), .tregsel(insrtuction_register_1_tregsel), .opcode(opcode));
  Register_File register_file_1 (
    .dwrite(dwrite), .regval(multiplexer_3_out), .sreg(sreg), .treg(treg),
    .dsel(insrtuction_register_1_dregsel), .ssel(insrtuction_register_1_sregsel),
    .tsel(insrtuction_register_1_tregsel), .R0(register_file_1_r0), .R1(register_file_1_r1),
    .R2(register_file_1_r2), .R7(register_file_1_r7), .R6(register_file_1_r6), .R5(register_file_1_r5),
    .R4(register_file_1_r4), .R3(register_file_1_r3), .dreg(dreg), .swrite(swrite));  // open: twrite
  // Probe on register_file_1_r0
  // Probe on register_file_1_r1
  // Probe on register_file_1_r2
  // Probe on register_file_1_r3
  // Probe on register_file_1_r4
  // Probe on register_file_1_r5
  // Probe on register_file_1_r6
  // Probe on register_file_1_r7
  // Probe on insrtuction_register_1_dregsel
  // Probe on insrtuction_register_1_sregsel
  // Probe on insrtuction_register_1_tregsel
  // Probe on opcode
  Multiplexer #(.select(2), .width(16), .enable("false")) multiplexer_4 (
    .in0(treg), .in1(immed), .in2({16{1'b0}}), .in3({16{1'b0}}), .out(multiplexer_4_out), .sel(op2sel));
  // Probe on aluop
  ALU alu_1 (.Zero(z), .Negative(n), .Result(aluout), .aluop(aluop), .A(sreg), .B(multiplexer_4_out), .Carry(c));
  // Probe on aluout

  // Notes on the sheet:
  //   16-bit CPU
  //   RAM
  //   Control Unit
  //   Immed
  //   PC
  //   IR
  //   Regs
  //   ALU
endmodule

module Insrtuction_Register (
  input  [15:0] instruction,
  input  irload,
  output [2:0] dregsel,
  output [2:0] sregsel,
  output [2:0] tregsel,
  output [6:0] opcode
);

  wire clock_1_out;

  Register #(.width(16)) IR (
    .D(instruction), .en(irload), .Q({opcode, tregsel, sregsel, dregsel}), .clk(clock_1_out));  // open: clr
  Clock clock_1 (.out(clock_1_out));

  // Notes on the sheet:
  //   Instruction Register 
endmodule

module Register_File (
  input  [15:0] regval,
  input  dwrite,
  input  swrite,
  input  twrite,
  input  [2:0] dsel,
  input  [2:0] ssel,
  input  [2:0] tsel,
  output [15:0] R0,
  output [15:0] R1,
  output [15:0] R2,
  output [15:0] R3,
  output [15:0] R4,
  output [15:0] R5,
  output [15:0] R6,
  output [15:0] R7,
  output [15:0] dreg,
  output [15:0] sreg,
  output [15:0] treg
);

  wire clock_1_out, demultiplexer_1_out0, demultiplexer_1_out1, demultiplexer_1_out2, demultiplexer_1_out3,
       demultiplexer_1_out4, demultiplexer_1_out5, demultiplexer_1_out6, demultiplexer_1_out7;

  Demultiplexer #(.select(3), .enable("false")) demultiplexer_1 (
    .out0(demultiplexer_1_out0), .out1(demultiplexer_1_out1), .out2(demultiplexer_1_out2),
    .out3(demultiplexer_1_out3), .out4(demultiplexer_1_out4), .out5(demultiplexer_1_out5),
    .out6(demultiplexer_1_out6), .out7(demultiplexer_1_out7), .in(dwrite), .sel(dsel));
  Demultiplexer #(.select(3), .enable("false")) demultiplexer_2 (
    .out0(demultiplexer_1_out0), .out1(demultiplexer_1_out1), .out2(demultiplexer_1_out2),
    .out3(demultiplexer_1_out3), .out4(demultiplexer_1_out4), .out5(demultiplexer_1_out5),
    .out6(demultiplexer_1_out6), .out7(demultiplexer_1_out7), .in(swrite), .sel(ssel));
  Demultiplexer #(.select(3), .enable("false")) demultiplexer_3 (
    .out0(demultiplexer_1_out0), .out1(demultiplexer_1_out1), .out2(demultiplexer_1_out2),
    .out3(demultiplexer_1_out3), .out4(demultiplexer_1_out4), .out5(demultiplexer_1_out5),
    .out6(demultiplexer_1_out6), .out7(demultiplexer_1_out7), .in(twrite), .sel(tsel));
  Register #(.width(16)) register_1 (.D(regval), .en(demultiplexer_1_out0), .Q(R0), .clk(clock_1_out));  // open: clr
  Register #(.width(16)) register_2 (.D(regval), .en(demultiplexer_1_out1), .Q(R1), .clk(clock_1_out));  // open: clr
  Register #(.width(16)) register_3 (.D(regval), .en(demultiplexer_1_out2), .Q(R2), .clk(clock_1_out));  // open: clr
  Register #(.width(16)) register_4 (.D(regval), .en(demultiplexer_1_out3), .Q(R3), .clk(clock_1_out));  // open: clr
  Register #(.width(16)) register_5 (.D(regval), .en(demultiplexer_1_out4), .Q(R4), .clk(clock_1_out));  // open: clr
  Register #(.width(16)) register_6 (.D(regval), .en(demultiplexer_1_out5), .Q(R5), .clk(clock_1_out));  // open: clr
  Register #(.width(16)) register_7 (.D(regval), .en(demultiplexer_1_out6), .Q(R6), .clk(clock_1_out));  // open: clr
  Register #(.width(16)) register_8 (.D(regval), .en(demultiplexer_1_out7), .Q(R7), .clk(clock_1_out));  // open: clr
  Clock clock_1 (.out(clock_1_out));
  Multiplexer #(.select(3), .width(16), .enable("false")) multiplexer_1 (
    .in0(R0), .in1(R1), .in2(R2), .in3(R3), .in4(R4), .in5(R5), .in6(R6), .in7(R7), .out(dreg), .sel(dsel));
  Multiplexer #(.select(3), .width(16), .enable("false")) multiplexer_2 (
    .in0(R0), .in1(R1), .in2(R2), .in3(R3), .in4(R4), .in5(R5), .in6(R6), .in7(R7), .out(sreg), .sel(ssel));
  Multiplexer #(.select(3), .width(16), .enable("false")) multiplexer_3 (
    .in0(R0), .in1(R1), .in2(R2), .in3(R3), .in4(R4), .in5(R5), .in6(R6), .in7(R7), .out(treg), .sel(tsel));

  // Notes on the sheet:
  //   Register File
endmodule

module ALU (
  input  [15:0] A,
  input  [15:0] B,
  input  [3:0] aluop,
  output Carry,
  output Zero,
  output Negative,
  output [15:0] Result
);

  wire adder_1_cout, or_2_out, subtractor_1_bout;
  wire [15:0] adder_1_out, and_1_out, divider_1_out, divider_1_rem, multiplier_1_out, nand_1_out, nor_1_out,
       or_1_out, subtractor_1_out, xor_1_out;

  Adder #(.width(16)) adder_1 (.a(A), .b(B), .out(adder_1_out), .cin(1'b0), .cout(adder_1_cout));
  Subtractor #(.width(16)) subtractor_1 (.a(A), .b(B), .out(subtractor_1_out), .bin(1'b0), .bout(subtractor_1_bout));
  Multiplier #(.width(16)) multiplier_1 (.a(A), .b(B), .out(multiplier_1_out), .cin({16{1'b0}}));  // open: cout
  Divider #(.width(16)) divider_1 (.a(A), .b(B), .out(divider_1_out), .upper({16{1'b0}}), .rem(divider_1_rem));
  assign and_1_out = A & B;  // AND_Gate and_1, 16 bits wide
  assign or_1_out = A | B;  // OR_Gate or_1, 16 bits wide
  assign xor_1_out = A ^ B;  // XOR_Gate xor_1, 16 bits wide
  assign nand_1_out = ~(A & B);  // NAND_Gate nand_1, 16 bits wide
  assign nor_1_out = ~(A | B);  // NOR_Gate nor_1, 16 bits wide
  Multiplexer #(.select(4), .width(16), .enable("false")) multiplexer_1 (
    .in0(adder_1_out), .in1(subtractor_1_out), .in2(multiplier_1_out), .in3(divider_1_out),
    .in4(divider_1_rem), .in5(and_1_out), .in6(or_1_out), .in7(xor_1_out), .in8(nand_1_out), .in9(nor_1_out),
    .out({Negative, Result[14:0]}), .sel(aluop));  // open: in10, in11, in12, in13, in14, in15
  Multiplexer #(.select(4), .enable("false")) multiplexer_2 (
    .in0(adder_1_cout), .in1(subtractor_1_bout), .in2(1'b0), .in3(1'b0), .in4(1'b0), .in5(1'b0), .in6(1'b0),
    .in7(1'b0), .in8(1'b0), .in9(1'b0), .in10(1'b0), .in11(1'b0), .in12(1'b0), .in13(1'b0), .in14(1'b0),
    .in15(1'b0), .out(Carry), .sel(aluop));
  or or_2 (or_2_out, Result[0], Result[1], Result[2], Result[3], Result[4], Result[5], Result[6], Result[7], Result[9], Result[10], Result[11], Result[12], Result[13], Result[14], Negative, Result[8]);
  not not_1 (Zero, or_2_out);

  assign Result[15] = Negative;

  // Notes on the sheet:
  //   16-bit ALU
endmodule

module Program_Counter (
  input  [15:0] imreg,
  input  pcload,
  input  reset,
  input  [1:0] pcsel,
  output [15:0] pcout
);

  wire clock_1_out;
  wire [15:0] adder_1_out, multiplexer_1_out;

  Adder #(.width(16)) adder_1 (.a(pcout), .b(16'h1), .out(adder_1_out));  // open: cin, cout
  Multiplexer #(.select(2), .width(16), .enable("false")) multiplexer_1 (
    .in0(adder_1_out), .in1(imreg), .out(multiplexer_1_out), .sel(pcsel));  // open: in2, in3
  Clock clock_1 (.out(clock_1_out));
  Register #(.width(16)) PC (.D(multiplexer_1_out), .en(pcload), .Q(pcout), .clk(clock_1_out), .clr(reset));

  // Notes on the sheet:
  //   Program Counter
endmodule

module Control_Unit (
  input  [6:0] opcode,
  output [3:0] aluop,
  output [1:0] op2sel,
  output datawrite,
  output [7:0] ucounter,
  output [1:0] addrsel,
  output [1:0] pcsel,
  output pcload,
  output dwrite,
  output irload,
  output imload,
  output [1:0] regsrc,
  output [1:0] datasel,
  output swrite
);

  wire clock_1_out, indexsel;
  wire [1:0] cond;
  wire [7:0] adder_1_out, multiplexer_1_out, multiplexer_2_out;
  wire [15:0] rom_2_data;
  wire [31:23] rom_1_data;

  Clock clock_1 (.out(clock_1_out));
  Register Microcounter (.D(adder_1_out), .Q(ucounter), .clk(clock_1_out));  // open: en, clr
  ROM #(.dataWidth(32)) rom_1 (
    .addr(ucounter),
    .data({rom_1_data, swrite, datasel, indexsel, cond, regsrc, imload, irload, dwrite, pcload, pcsel, addrsel, datawrite, op2sel, aluop}));  // open: sel
  ROM #(.dataWidth(16)) rom_2 (.addr(ucounter), .data(rom_2_data));  // open: sel
  Multiplexer #(.width(8), .enable("false")) multiplexer_1 (
    .in0({8{1'b0}}), .in1({1'b0, opcode}), .out(multiplexer_1_out), .sel(indexsel));
  Multiplexer #(.width(8), .enable("false")) multiplexer_2 (
    .in0(rom_2_data[7:0]), .in1(rom_2_data[15:8]), .out(multiplexer_2_out), .sel(1'b0));
  Adder adder_1 (.a(multiplexer_2_out), .b(multiplexer_1_out), .out(adder_1_out));  // open: cin, cout

  // Notes on the sheet:
  //   Control Unit
  //   Rom1
  //   Rom2
  //   contents of rom_1 (hex, n*v repeats v):
  //   2000 80800 11000 11001 11002 11003 11004 11005 11006 11007 11008 11009 30*0 4000 22*0 1000 0 4000
  //   62*0 21 800 1000c0 800 800 a00
  //   contents of rom_2 (hex, n*v repeats v):
  //   101 202 40*0 8282 22*0 8383 0 8484 62*0 8687 0 8585
endmodule
